# Fritzing sketch AR05_4led (saved by Fritzing 0.9.3b)
breadboards: 1

parts:
  부품1 = Arduino Uno (Rev3)
  R2 = Resistor [tolerance=±5% resistance=220 package=THT]
  R3 = Resistor [tolerance=±5% resistance=220 package=THT]
  R4 = Resistor [tolerance=±5% resistance=220 package=THT]
  R5 = Resistor [tolerance=±5% resistance=220 package=THT]
  LED1 = LED - 5mm [color="Yellow (595nm)" package="5 mm [THT]"]
  LED2 = LED - 5mm [color="Blue (430nm)" package="5 mm [THT]"]
  LED4 = LED - 5mm [color="Red (633nm)" package="5 mm [THT]"]
  LED5 = LED - 5mm [color="Blue (525nm)" package="5 mm [THT]"]

nets:
  N1: 부품1.D9_PWM, LED1.anode
  N2: 부품1.D3_PWM, LED4.anode
  N3: 부품1.D5_PWM, LED5.anode
  N4: 부품1.D6_PWM, LED2.anode
  N5: 부품1.GND, R2.Pin_1, R3.Pin_1, R4.Pin_1, R5.Pin_1
  N6: R2.Pin_0, LED2.cathode
  N7: R3.Pin_0, LED1.cathode
  N8: R4.Pin_0, LED5.cathode
  N9: R5.Pin_0, LED4.cathode
