# Fritzing sketch AR05_FND1 (saved by Fritzing 0.9.3b)
breadboards: 1

parts:
  부품1 = Arduino Uno (Rev3)
  R1 = Resistor [tolerance=±5% resistance=220 package=THT]
  R2 = Resistor [tolerance=±5% resistance=220 package=THT]
  R3 = Resistor [tolerance=±5% resistance=220 package=THT]
  R4 = Resistor [tolerance=±5% resistance=220 package=THT]
  R5 = Resistor [tolerance=±5% resistance=220 package=THT]
  R6 = Resistor [tolerance=±5% resistance=220 package=THT]  # not connected
  R7 = Resistor [tolerance=±5% resistance=220k package=THT]
  R8 = Resistor [tolerance=±5% resistance=220 package=THT]
  7_Segment1 = 7 Segment Display

nets:
  N1: 부품1.D8, R7.Pin_1
  N2: 부품1.D9_PWM, R3.Pin_0
  N3: 부품1.D2, R1.Pin_1
  N4: 부품1.D3_PWM, R2.Pin_1
  N5: 부품1.D4, R4.Pin_0
  N6: 부품1.D6_PWM, R5.Pin_0
  N7: 부품1.D7, R8.Pin_1
  N8: 부품1.GND, 7_Segment1.common_cathode
  N9: R1.Pin_0, 7_Segment1.Segment_A#10
  N10: R2.Pin_0, 7_Segment1.Segment_B
  N11: R3.Pin_1, 7_Segment1.Segment_DP
  N12: R4.Pin_1, 7_Segment1.Segment_C
  N13: R5.Pin_1, 7_Segment1.Segment_E
  N14: R7.Pin_0, 7_Segment1.Segment_F
  N15: R8.Pin_0, 7_Segment1.Segment_A#1
